# Fritzing sketch magicballs (saved by Fritzing 0.9.2b)

parts:
  blah1 = Raspberry Pi Zero
  C3 = LSM303DLHC
  C4 = Microstack GPS

nets:
  N1: blah1.3.3v#8, C3.3V3
  N2: blah1.GPIO2_(SDA1), C3.SDA
  N3: blah1.GPIO3_(SCL), C3.SCL
  N4: blah1.Ground#13, C3.GND
  N5: blah1.GPIO4_(GCLK), C4.PPS
  N6: blah1.GPIO14_(TXD0), C4.MTXSRX
  N7: blah1.GPIO15_(RXD0), C4.MRXSTX
  N8: blah1.GPIO18_(GEN1), C4.Wake
  N9: blah1.3.3v#24, C4.*3V3
  N10: blah1.Ground#46, C4.Gnd

custom parts:
  LSM303DLHC: Cheap 3-axis accelerometer, altimeter and magnetometer
  Microstack GPS: Microstack GPS module
